# Fritzing sketch MotorSchematic (saved by Fritzing 0.9.1b)
breadboards: 1

parts:
  Raspberry_Pi1 = Raspberry Pi B rev2
  IC1 = L293D [package=THT]

nets:
  N1: Raspberry_Pi1.5V, IC1.+V
  N2: Raspberry_Pi1.GPIO_14, IC1.Enable_1
  N3: Raspberry_Pi1.GPIO_15, IC1.In_1
  N4: Raspberry_Pi1.GPIO_18, IC1.In_2
